# Fritzing sketch ProjectSketchV1 (saved by Fritzing 0.9.3b)
breadboards: 1

parts:
  J1 = Basic Servo
  J4 = Basic Servo
  J5 = Basic Servo
  J6 = Basic Servo
  元件1 = Arduino Uno (Rev3)
  J3 = Basic Servo
  J7 = Basic Servo
  U3 = RELAY [package=relay-jzc]
  U4 = RELAY [package=relay-jzc]
  R1 = Resistor [tolerance=±5% resistance=220 package=THT]
  S2 = Round Pushbutton
  S3 = Round Pushbutton
  M1 = DC Motor  # not connected
  R2 = Resistor [tolerance=±5% resistance=220 package=THT]
  GY2 = MPU-6050 Board GY-521 [form="♀ (female)" package=THT]

nets:
  GND: J1.gnd, J4.gnd, J5.gnd, J6.gnd, 元件1.GND, J3.gnd, J7.gnd
  VCC: J1.vcc, J4.vcc, J5.vcc, J6.vcc, J3.vcc, J7.vcc
  N1: J4.pulse, 元件1.D9_PWM
  N2: J5.pulse, 元件1.D3_PWM
  N3: J6.pulse, 元件1.D5_PWM
  N4: 元件1.A4/SDA, GY2.pin4
  N5: 元件1.A5/SCL, GY2.pin3
  N6: 元件1.D10_PWM/SS, J3.pulse
  N7: 元件1.D11_PWM/MOSI, J7.pulse
  N8: 元件1.D12/MISO, U3.NC, U4.NC
  N9: 元件1.D13/SCK, U3.COIL2, U4.COIL2
  N10: 元件1.D2, R1.Pin_1, S3.leg1
  N11: 元件1.D4, S2.leg1, R2.Pin_1
  N12: 元件1.5V, U3.NO, U4.NO
  N13: R1.Pin_0, R2.Pin_0, GY2.pin2
  N14: S2.leg0, S3.leg0, GY2.pin1

notes:
  [Linear actuator]
  mini servo motors in the hand
  servo motor on the wrist
  2 relay module
  hand control button
  linear actuator permanent control button
  power connection
  gyroscope MPU6050

custom parts:
  MPU-6050 Board GY-521: Acelerometro y Giroscopio MPU-6050 Board GY-521
